// Digital circuit 1. BCD-7SegmentDisplay.dig as structural Verilog
module _1__BCD_7SegmentDisplay (
  input  A,
  input  B,
  input  C,
  input  D,
  input  in_5
);

  wire and_1_out, and_2_out, and_3_out, and_4_out, and_5_out, and_6_out, and_7_out, and_8_out, and_9_out,
       and_10_out, and_11_out, and_12_out, and_13_out, and_14_out, and_15_out, and_16_out, and_17_out,
       and_18_out, not_1_out, not_2_out, not_3_out, not_4_out, not_5_out, not_6_out, not_7_out, not_8_out,
       not_9_out, not_10_out, not_11_out, not_12_out, not_13_out, not_14_out, not_15_out, not_16_out,
       not_17_out, not_18_out, not_19_out, not_20_out, not_21_out, not_22_out, not_23_out, not_24_out,
       not_25_out, not_26_out, not_27_out, or_1_out, or_2_out, or_3_out, or_4_out, or_5_out, or_6_out,
       or_7_out;

  not not_1 (not_1_out, C);
  not not_2 (not_2_out, C);
  not not_3 (not_3_out, D);
  not not_4 (not_4_out, B);
  not not_5 (not_5_out, C);
  not not_6 (not_6_out, D);
  and and_1 (and_1_out, B, D);
  and and_2 (and_2_out, C, not_7_out);
  not not_7 (not_7_out, A);
  not not_8 (not_8_out, B);
  and and_3 (and_3_out, not_8_out, not_9_out, not_10_out, A);
  not not_9 (not_9_out, C);
  not not_10 (not_10_out, D);
  and and_4 (and_4_out, B, D);
  not not_11 (not_11_out, B);
  and and_5 (and_5_out, not_11_out, C, A);
  not not_12 (not_12_out, A);
  and and_6 (and_6_out, not_12_out, B, C);
  and and_7 (and_7_out, D, B);
  not not_13 (not_13_out, C);
  and and_8 (and_8_out, not_13_out, B, not_14_out);
  not not_14 (not_14_out, A);
  and and_9 (and_9_out, D, A);
  and and_10 (and_10_out, A, not_15_out, not_16_out);
  not not_15 (not_15_out, B);
  not not_16 (not_16_out, C);
  not not_17 (not_17_out, A);
  and and_11 (and_11_out, not_17_out, not_18_out, C);
  not not_18 (not_18_out, B);
  and and_12 (and_12_out, A, B, C);
  not not_19 (not_19_out, B);
  and and_13 (and_13_out, not_19_out, C);
  and and_14 (and_14_out, A, B);
  and and_15 (and_15_out, not_1_out, B);
  and and_16 (and_16_out, A, not_2_out, not_3_out);
  and and_17 (and_17_out, A, B, C);
  and and_18 (and_18_out, not_4_out, not_5_out, not_6_out);
  or or_1 (or_1_out, and_1_out, and_2_out, and_3_out);
  or or_2 (or_2_out, and_4_out, and_5_out, and_6_out);
  or or_3 (or_3_out, and_7_out, and_8_out);
  or or_4 (or_4_out, and_13_out, A);
  or or_5 (or_5_out, and_14_out, and_15_out, and_16_out);
  or or_6 (or_6_out, and_17_out, and_18_out);
  or or_7 (or_7_out, and_9_out, and_10_out, and_11_out, and_12_out);
  not not_20 (not_20_out, or_1_out);
  not not_21 (not_21_out, or_2_out);
  not not_22 (not_22_out, or_3_out);
  not not_23 (not_23_out, or_7_out);
  Seven_Seg seven_seg_1 (
    .a(not_20_out), .b(not_21_out), .c(not_22_out), .d(not_23_out), .e(not_24_out), .f(not_25_out),
    .g(not_26_out), .dp(not_27_out));
  not not_24 (not_24_out, or_4_out);
  not not_25 (not_25_out, or_5_out);
  not not_26 (not_26_out, or_6_out);
  not not_27 (not_27_out, in_5);
endmodule
