// Digital circuit 7.1 - UnaEUnaSolaB.dig as structural Verilog
module _7_1___UnaEUnaSolaB (
  input  X2,
  input  X1,
  output Z
);

  wire and_1_out, and_2_out, and_3_out, and_4_out, and_5_out, and_6_out, and_7_out, and_8_out, and_9_out,
       and_10_out, and_11_out, and_12_out, and_13_out, and_14_out, not_1_out, not_2_out, not_3_out,
       not_4_out, not_5_out, or_1_out, or_2_out, or_3_out, reset_1_out;

  not not_1 (not_1_out, X2);
  not not_2 (not_2_out, X1);
  not not_3 (not_3_out, and_12_out);
  not not_4 (not_4_out, and_13_out);
  not not_5 (not_5_out, and_14_out);
  and and_1 (and_1_out, and_12_out, not_1_out);
  and and_2 (and_2_out, and_13_out, not_1_out, X1);
  and and_3 (and_3_out, and_14_out, X1);
  and and_4 (and_4_out, and_14_out, X2);
  and and_5 (and_5_out, and_12_out, and_13_out);
  and and_6 (and_6_out, and_13_out, X2, not_2_out);
  and and_7 (and_7_out, not_1_out, X1);
  and and_8 (and_8_out, and_14_out, X1);
  and and_9 (and_9_out, and_14_out, not_1_out);
  and and_10 (and_10_out, not_3_out, and_13_out);
  and and_11 (and_11_out, not_3_out, and_14_out);
  or or_1 (or_1_out, and_1_out, and_2_out);
  or or_2 (or_2_out, and_12_out, and_3_out, and_4_out, and_5_out, and_6_out);
  or or_3 (or_3_out, and_12_out, and_7_out, and_8_out, and_9_out);
  or or_4 (Z, and_10_out, and_11_out);
  Reset reset_1 (.out(reset_1_out));
  and and_12 (and_12_out, or_1_out, reset_1_out);
  and and_13 (and_13_out, or_2_out, reset_1_out);
  and and_14 (and_14_out, reset_1_out, or_3_out);

  // Notes on the sheet:
  //   y2
  //   y1
  //   y0
endmodule
