// Digital circuit 7.2 - PT.dig as structural Verilog
module _7_2___PT (
  input  X2,
  input  X1,
  output Z
);

  wire and_1_out, and_2_out, and_4_out, and_5_out, and_6_out, and_7_out, not_1_out, not_2_out, not_3_out,
       not_4_out, not_5_out, or_1_out, or_2_out, or_3_out, or_4_out, or_5_out, or_6_out, or_7_out, or_8_out,
       reset_1_out;

  not not_1 (not_1_out, X2);
  not not_2 (not_2_out, X1);
  not not_3 (not_3_out, and_5_out);
  not not_4 (not_4_out, and_6_out);
  not not_5 (not_5_out, and_7_out);
  or or_1 (or_1_out, X2, X1);
  or or_2 (or_2_out, and_6_out, X2);
  or or_3 (or_3_out, and_5_out, not_1_out);
  or or_4 (or_4_out, and_5_out, and_6_out);
  or or_5 (or_5_out, and_5_out, X1);
  or or_6 (or_6_out, and_6_out, not_2_out);
  or or_7 (or_7_out, and_6_out, and_7_out, X1);
  or or_8 (or_8_out, not_1_out, X1, not_3_out);
  and and_1 (and_1_out, or_6_out, not_1_out);
  and and_2 (and_2_out, or_7_out, or_8_out);
  and and_3 (Z, not_4_out, and_7_out, not_3_out);
  and and_4 (and_4_out, or_1_out, or_2_out, or_3_out, or_4_out, or_5_out, and_7_out);
  Reset reset_1 (.out(reset_1_out));
  and and_5 (and_5_out, and_4_out, reset_1_out);
  and and_6 (and_6_out, and_1_out, reset_1_out);
  and and_7 (and_7_out, reset_1_out, and_2_out);

  // Notes on the sheet:
  //   y2
  //   y1
  //   y0
endmodule
