// Digital circuit 7.3 - Es1.dig as structural Verilog
module _7_3___Es1 (
  input  C,
  input  A,
  output Z
);

  wire and_1_out, and_2_out, nand_1_out, nand_2_out, nand_3_out, nand_4_out, nand_5_out, nand_6_out,
       nand_8_out, nand_9_out, nand_10_out, reset_1_out;

  // Not not_1 has open pins: in=C, out=open
  // Not not_2 has open pins: in=A, out=open
  // Not not_3 has open pins: in=and_2_out, out=open
  // Not not_4 has open pins: in=and_1_out, out=open
  nand nand_1 (nand_1_out, and_1_out, and_1_out);
  nand nand_2 (nand_2_out, and_2_out, and_2_out);
  nand nand_3 (nand_3_out, A, A);
  nand nand_4 (nand_4_out, and_2_out, and_1_out);
  nand nand_5 (nand_5_out, C, and_1_out);
  nand nand_6 (nand_6_out, C, A);
  nand nand_7 (Z, nand_1_out, nand_2_out);
  nand nand_8 (nand_8_out, nand_3_out, and_1_out);
  nand nand_9 (nand_9_out, nand_5_out, nand_6_out);
  Reset reset_1 (.out(reset_1_out));
  nand nand_10 (nand_10_out, nand_8_out, nand_4_out);
  and and_1 (and_1_out, nand_9_out, reset_1_out);
  and and_2 (and_2_out, reset_1_out, nand_10_out);

  // Notes on the sheet:
  //   y1
  //   y0
endmodule
