// Digital circuit 7.3 - Es8.dig as structural Verilog
module _7_3___Es8 (
  input  S,
  input  C,
  output Q
);

  wire and_1_out, and_2_out, and_3_out, and_4_out, and_6_out, and_7_out, not_1_out, not_2_out, not_3_out,
       or_1_out, or_2_out, reset_1_out;

  not not_1 (not_1_out, S);
  not not_2 (not_2_out, C);
  not not_3 (not_3_out, and_7_out);
  // Not not_4 has open pins: in=and_6_out, out=open
  and and_1 (and_1_out, and_6_out, not_1_out);
  and and_2 (and_2_out, and_6_out, not_1_out, not_2_out);
  and and_3 (and_3_out, and_7_out, not_1_out);
  and and_4 (and_4_out, C, and_7_out);
  and and_5 (Q, C, not_3_out);
  or or_1 (or_1_out, and_1_out, C);
  or or_2 (or_2_out, and_2_out, and_3_out, and_4_out);
  Reset reset_1 (.out(reset_1_out));
  and and_6 (and_6_out, reset_1_out, or_1_out);
  and and_7 (and_7_out, reset_1_out, or_2_out);

  // Notes on the sheet:
  //   y1
  //   y0
endmodule
